# Fritzing sketch coeur de LED (saved by Fritzing 0.9.3b)
breadboards: 1

parts:
  Composant1 = Arduino Uno (Rev3)
  LED10 = LED - 5mm [color="Red (633nm)" package="5 mm [THT]"]
  LED6 = LED - 5mm [color="Red (633nm)" package="5 mm [THT]"]
  LED1 = LED - 5mm [color="Red (633nm)" package="5 mm [THT]"]
  LED9 = LED - 5mm [color="Red (633nm)" package="5 mm [THT]"]
  LED8 = LED - 5mm [color="Red (633nm)" package="5 mm [THT]"]
  LED2 = LED - 5mm [color="Red (633nm)" package="5 mm [THT]"]
  R6 = Resistor [tolerance=±5% resistance=220 package=THT]
  R7 = Resistor [tolerance=±5% resistance=220 package=THT]
  R3 = Resistor [tolerance=±5% resistance=220 package=THT]
  R5 = Resistor [tolerance=±5% resistance=220 package=THT]
  R4 = Resistor [tolerance=±5% resistance=220 package=THT]
  LED3 = LED - 5mm [color="Red (633nm)" package="5 mm [THT]"]
  R2 = Resistor [tolerance=±5% resistance=220 package=THT]
  R1 = Resistor [tolerance=±5% resistance=220 package=THT]
  LED4 = LED - 5mm [color="Red (633nm)" package="5 mm [THT]"]
  R9 = Resistor [tolerance=±5% resistance=220 package=THT]
  LED7 = LED - 5mm [color="Red (633nm)" package="5 mm [THT]"]
  R8 = Resistor [tolerance=±5% resistance=47 package=THT]

nets:
  N1: Composant1.D8, R4.Pin_0
  N2: Composant1.D9_PWM, R6.Pin_0
  N3: Composant1.D10_PWM/SS, R9.Pin_0
  N4: Composant1.D11_PWM/MOSI, R2.Pin_1
  N5: Composant1.D12/MISO, R3.Pin_0
  N6: Composant1.D13/SCK, R5.Pin_1
  N7: Composant1.GND, LED10.cathode, LED6.cathode, LED1.cathode, LED9.cathode, LED8.cathode, LED2.cathode, LED3.cathode, LED4.cathode, LED7.cathode
  N8: Composant1.D5_PWM, R1.Pin_1
  N9: Composant1.D6_PWM, R7.Pin_1
  N10: Composant1.D7, R8.Pin_1
