# Fritzing sketch Module cardio (saved by Fritzing 0.9.3b)
breadboards: 1

parts:
  Composant1 = Arduino Uno (Rev3)
  R1 = Resistor [tolerance=±5% resistance=100 package=THT]
  R2 = Resistor [tolerance=±5% resistance=22k package=THT]
  LED1 = LED - 5mm [color="Infrared (940nm)" package="5 mm [THT]"]
  R3 = Resistor [tolerance=±5% resistance=68k package=THT]
  U1 = LM124-324 Quad Opamp [package="DIP (Dual Inline)"]
  R4 = Resistor [tolerance=±5% resistance=1k package=THT]
  C1 = Ceramic Capacitor [capacitance=100nF package="100 mil [THT, multilayer]"]
  R5 = Resistor [tolerance=±5% resistance=470k package=THT]
  R6 = Resistor [tolerance=±5% resistance=100 package=THT]
  LED2 = LED - 5mm [color="Red (633nm)" package="5 mm [THT]"]
  R7 = PHOTOCELL [package=photocell]
  CS = Ceramic Capacitor [capacitance=1µF package="100 mil [THT, multilayer]"]

nets (from the schematic view):
  N1: Composant1.A0, R6.Pin_1
  N2: Composant1.GND, LED1.cathode, R3.Pin_1, U1.VCC-, R4.Pin_0, LED2.cathode, LED2.anode, R7.P$2
  N3: Composant1.5V, R1.Pin_0, R2.Pin_0, U1.VCC+
  N4: R1.Pin_1, LED1.anode
  N5: R2.Pin_1, R7.P$1, CS.1
  N6: R3.Pin_0, U1.2IN+, CS.0
  N7: U1.2IN-, R4.Pin_1, C1.1, R5.Pin_0
  N8: U1.2OUT, C1.0, R5.Pin_1, R6.Pin_0

// code stored in the sketch: mainArduino.ino
/*inclusion des bibliotheques necessaires au programme*/
#include "cardio.h"



void setup() {
/*selection du port de l'arduino utilise pour l'entree de donnees*/
pinMode(pinDuCapteur, INPUT);
/*choix du nombre de baud a 9600*/
Serial.begin(9600);
}

void loop() {
/*definition de la variable pulse a 0*/
pulse=0;
/*fonction millis() qui permet de calculer la duree ecoulee depuis le lancement du programme*/
millistart2= millis();
while (millis()<millistart2+10000)
{
 /*utilisation de la fonction traitement*/
 pulse=traitement()+pulse;

  
/*duree de 10 secondes entre chaque boucle*/
 delay(10);
}
millisEnd=millis();      

/*formule de calcul du poul*/
resultat=pulse*6;
/*affichage du poul calcule*/
Serial.println(resultat);

/*fin du compteur de duree ecoulee*/
millisEnd = millis();
millisEnd=millisEnd;
/*affichage de la duree ecoulee*/
Serial.println(millisEnd);





}
