# Fritzing sketch coeur de LED (saved by Fritzing 0.9.3b)
breadboards: 1

parts:
  R3 = Resistor [tolerance=±5% resistance=220 package=THT]
  Composant2 = Arduino Uno (Rev3)
  LED7 = LED - 5mm [color="Red (633nm)" package="5 mm [THT]"]
  LED10 = LED - 5mm [color="Red (633nm)" package="5 mm [THT]"]
  LED13 = LED - 5mm [color="Red (633nm)" package="5 mm [THT]"]
  R4 = Resistor [tolerance=±5% resistance=220 package=THT]
  R5 = Resistor [tolerance=±5% resistance=220 package=THT]
  R6 = Resistor [tolerance=±5% resistance=220 package=THT]
  R7 = Resistor [tolerance=±5% resistance=220 package=THT]
  R8 = Resistor [tolerance=±5% resistance=220 package=THT]
  R9 = Resistor [tolerance=±5% resistance=220 package=THT]
  LED16 = LED - 5mm [color="Red (633nm)" package="5 mm [THT]"]
  LED17 = LED - 5mm [color="Red (633nm)" package="5 mm [THT]"]
  LED19 = LED - 5mm [color="Red (633nm)" package="5 mm [THT]"]
  LED20 = LED - 5mm [color="Red (633nm)" package="5 mm [THT]"]
  R12 = Resistor [tolerance=±5% resistance=220 package=THT]
  R13 = Resistor [tolerance=±5% resistance=220 package=THT]
  LED22 = LED - 5mm [color="Red (633nm)" package="5 mm [THT]"]
  LED23 = LED - 5mm [color="Red (633nm)" package="5 mm [THT]"]

nets:
  N1: R3.Pin_0, LED10.cathode
  N2: R3.Pin_1, Composant2.D5_PWM
  N3: Composant2.D8, R9.Pin_0
  N4: Composant2.D9_PWM, R13.Pin_1
  N5: Composant2.D10_PWM/SS, R12.Pin_1
  N6: Composant2.D11_PWM/MOSI, R5.Pin_1
  N7: Composant2.D12/MISO, R4.Pin_1
  N8: Composant2.D13/SCK, R6.Pin_1
  N9: Composant2.GND, LED10.anode, LED19.anode, LED23.anode
  N10: Composant2.D6_PWM, R7.Pin_0
  N11: Composant2.D7, R8.Pin_0
  N12: LED7.cathode, R4.Pin_0
  N13: LED7.anode, LED13.anode, LED16.anode, LED17.anode, LED20.anode, LED22.anode
  N14: LED13.cathode, R5.Pin_0
  N15: R6.Pin_0, LED23.cathode
  N16: R7.Pin_1, LED19.cathode
  N17: R8.Pin_1, LED16.cathode
  N18: R9.Pin_1, LED22.cathode
  N19: LED17.cathode, R12.Pin_0
  N20: LED20.cathode, R13.Pin_0
